// Logisim project alu.circ as structural Verilog: 1 circuit, main circuit alu
module alu (
  input  [31:0] A,
  input  [31:0] B,
  input  [3:0] ALUSel,
  output [31:0] Result
);

  wire and_2_out, and_3_out, and_4_out, and_5_out, comparator_1_lt;
  wire [1:0] and_6_out, and_7_out, and_8_out, and_9_out, bit_extender_2_out, bit_extender_3_out,
       bit_extender_4_out, bit_extender_5_out, or_2_out;
  wire [31:0] ABnegpos, ABposneg, add, adder_1_out, adder_2_out, multiplier_1_out, multiplier_2_out, myand,
       mydiv, mymul, mymulh, myor, myrem, mysll, myslt, mysra, mysrl, mysub, myxor, neg, negpos, not_1_out,
       not_2_out, not_3_out, not_4_out, not_5_out, not_6_out, pos, posneg;

  assign not_1_out = ~A;  // NOT_Gate not_1, 32 bits wide
  assign not_2_out = ~B;  // NOT_Gate not_2, 32 bits wide
  Multiplier #(.width(32)) multiplier_1 (.a(A), .b({32{1'b1}}), .out(multiplier_1_out));  // open: cin, cout
  Multiplier #(.width(32)) multiplier_2 (.a(B), .b({32{1'b1}}), .out(multiplier_2_out));  // open: cin, cout
  Adder #(.width(32)) adder_1 (.a(not_1_out), .b(32'h1), .out(adder_1_out));  // open: cin, cout
  Adder #(.width(32)) adder_2 (.a(not_2_out), .b(32'h1), .out(adder_2_out));  // open: cin, cout
  Adder #(.width(32)) adder_3 (.a(A), .b(B), .out(add));  // open: cin, cout
  assign myand = A & B;  // AND_Gate and_1, 32 bits wide
  assign myor = A | B;  // OR_Gate or_1, 32 bits wide
  assign myxor = A ^ B;  // XOR_Gate xor_1, 32 bits wide
  Shifter #(.width(32), .shift("lr")) shifter_1 (.in(A), .\dist (B[4:0]), .out(mysrl));
  Shifter #(.width(32), .shift("ar")) shifter_2 (.in(A), .\dist (B[4:0]), .out(mysra));
  Shifter #(.width(32)) shifter_3 (.in(A), .\dist (B[4:0]), .out(mysll));
  Multiplier #(.width(32)) multiplier_3 (.a(A), .b(B), .cout(posneg));  // open: out, cin
  Multiplier #(.width(32)) multiplier_4 (.a(A), .b(B), .cout(negpos));  // open: out, cin
  Adder #(.width(32)) adder_4 (.a(multiplier_1_out), .b(posneg), .out(ABposneg));  // open: cin, cout
  Adder #(.width(32)) adder_5 (.a(multiplier_2_out), .b(negpos), .out(ABnegpos));  // open: cin, cout
  Multiplier #(.width(32)) multiplier_5 (.a(A), .b(B), .cout(pos));  // open: out, cin
  Multiplier #(.width(32)) multiplier_6 (.a(adder_1_out), .b(adder_2_out), .cout(neg));  // open: out, cin
  // Probe on posneg
  // Probe on negpos
  Comparator #(.width(32)) comparator_1 (.a(A), .b(B), .lt(comparator_1_lt));  // open: gt, eq
  Divider #(.width(32)) divider_1 (.a(A), .b(B), .out(mydiv));  // open: upper, rem
  Divider #(.width(32)) divider_2 (.a(A), .b(B), .rem(myrem));  // open: out, upper
  Multiplier #(.width(32)) multiplier_7 (.a(A), .b(B), .out(mymul));  // open: cin, cout
  Subtractor #(.width(32)) subtractor_1 (.a(A), .b(B), .out(mysub));  // open: bin, bout
  // Probe on ABposneg
  // Probe on ABnegpos
  // Probe on pos
  // Probe on neg
  assign myslt = {{31{1'b0}}, comparator_1_lt};  // Bit_Extender bit_extender_1
  Multiplexer #(.select(4), .width(32), .enable("false")) multiplexer_1 (
    .in0(add), .in1(myand), .in2(myor), .in3(myxor), .in4(mysrl), .in5(mysra), .in6(mysll), .in7(myslt),
    .in8(mydiv), .in9(myrem), .in10(mymul), .in11(mymulh), .in12(mysub), .in13(B), .out(Result), .sel(ALUSel));  // open: in14, in15
  assign not_3_out = ~A;  // NOT_Gate not_3, 32 bits wide
  assign not_4_out = ~B;  // NOT_Gate not_4, 32 bits wide
  assign not_5_out = ~A;  // NOT_Gate not_5, 32 bits wide
  assign not_6_out = ~B;  // NOT_Gate not_6, 32 bits wide
  // Probe on and_2_out
  and and_2 (and_2_out, A[31], B[31]);
  and and_3 (and_3_out, not_3_out[31], B[31]);
  and and_4 (and_4_out, A[31], not_4_out[31]);
  and and_5 (and_5_out, not_5_out[31], not_6_out[31]);
  // Probe on and_5_out
  assign bit_extender_2_out = {{1{and_2_out}}, and_2_out};  // Bit_Extender bit_extender_2
  assign bit_extender_3_out = {{1{and_3_out}}, and_3_out};  // Bit_Extender bit_extender_3
  assign bit_extender_4_out = {{1{and_4_out}}, and_4_out};  // Bit_Extender bit_extender_4
  assign bit_extender_5_out = {{1{and_5_out}}, and_5_out};  // Bit_Extender bit_extender_5
  assign and_6_out = bit_extender_2_out & 2'b00;  // AND_Gate and_6, 2 bits wide
  // Probe on and_7_out
  assign and_7_out = bit_extender_3_out & 2'b01;  // AND_Gate and_7, 2 bits wide
  assign and_8_out = bit_extender_4_out & 2'b10;  // AND_Gate and_8, 2 bits wide
  // Probe on and_8_out
  assign and_9_out = bit_extender_5_out & 2'b11;  // AND_Gate and_9, 2 bits wide
  // Probe on and_6_out
  assign or_2_out = and_6_out | and_7_out | and_8_out | and_9_out;  // OR_Gate or_2, 2 bits wide
  // Probe on and_9_out
  Multiplexer #(.select(2), .width(32), .enable("false")) multiplexer_2 (
    .in0(neg), .in1(ABposneg), .in2(ABnegpos), .in3(pos), .out(mymulh), .sel(or_2_out));
  // Probe on or_2_out
  // Probe on mymulh

  // Other names for the same wires on the sheet: mybsel[31:0] = B

  // Notes on the sheet:
  //   INPUTS to your circuit
  //   DON'T CHANGE THE LOCATIONS OF THE INPUTS AND OUTPUTS!
  //   OUTPUT from your circuit
endmodule
