// Logisim project regfile.circ as structural Verilog: 1 circuit, main circuit main
module main (
  input  [4:0] Read_Register_1_rs1,
  input  [4:0] Read_Register_2_rs2,
  input  [4:0] Write_Register_rd,
  input  [31:0] Write_Data,
  input  Write_Enable,
  input  Clock,
  output [31:0] ra,
  output [31:0] sp,
  output [31:0] t0,
  output [31:0] t1,
  output [31:0] t2,
  output [31:0] s0,
  output [31:0] s1,
  output [31:0] a0,
  output [31:0] Read_Data_1,
  output [31:0] Read_Data_2
);

  wire demultiplexer_1_out1, demultiplexer_1_out2, demultiplexer_1_out5, demultiplexer_1_out6,
       demultiplexer_1_out7, demultiplexer_1_out8, demultiplexer_1_out9, demultiplexer_1_out10;
  wire [4:0] undriven_33;
  wire [31:0] multiplexer_2_out, undriven, undriven_2, undriven_3, undriven_4, undriven_5, undriven_6,
       undriven_7, undriven_8, undriven_9, undriven_10, undriven_11, undriven_12, undriven_13, undriven_14,
       undriven_15, undriven_16, undriven_17, undriven_18, undriven_19, undriven_20, undriven_21,
       undriven_22, undriven_23, undriven_24, undriven_25, undriven_26, undriven_27, undriven_28,
       undriven_29, undriven_30, undriven_31, undriven_32, undriven_34, undriven_35, undriven_36,
       undriven_37, undriven_38, undriven_39, undriven_40, undriven_41, undriven_42, undriven_43,
       undriven_44, undriven_45, undriven_46, undriven_47, undriven_48, undriven_49, undriven_50,
       undriven_51, undriven_52, undriven_53, undriven_54, undriven_55, undriven_56;

  Demultiplexer #(.select(5), .enable("false")) demultiplexer_1 (
    .out1(demultiplexer_1_out1), .out2(demultiplexer_1_out2), .out5(demultiplexer_1_out5),
    .out6(demultiplexer_1_out6), .out7(demultiplexer_1_out7), .out8(demultiplexer_1_out8),
    .out9(demultiplexer_1_out9), .out10(demultiplexer_1_out10), .in(Write_Enable), .sel(Write_Register_rd));  // open: out0, out3, out4, out11, out12, out13, out14, out15, out16, out17, out18, out19, out20, out21, out22, out23, out24, out25, out26, out27, out28, out29, out30, out31
  Register #(.width(32)) register_1 (.D(Write_Data), .en(demultiplexer_1_out1), .clk(Clock), .Q(ra));  // open: clr
  Register #(.width(32)) register_2 (.D(Write_Data), .en(demultiplexer_1_out5), .clk(Clock), .Q(t0));  // open: clr
  Register #(.width(32)) register_3 (.D(Write_Data), .en(demultiplexer_1_out7), .clk(Clock), .Q(t2));  // open: clr
  Register #(.width(32)) register_4 (.D(Write_Data), .en(demultiplexer_1_out8), .clk(Clock), .Q(s0));  // open: clr
  Register #(.width(32)) register_5 (.D(Write_Data), .en(demultiplexer_1_out9), .clk(Clock), .Q(s1));  // open: clr
  Register #(.width(32)) register_6 (.D(Write_Data), .en(demultiplexer_1_out10), .clk(Clock), .Q(a0));  // open: clr
  Register #(.width(32)) register_7 (.D(Write_Data), .en(demultiplexer_1_out2), .clk(Clock), .Q(sp));  // open: clr
  Register #(.width(32)) register_8 (.D(Write_Data), .en(demultiplexer_1_out6), .clk(Clock), .Q(t1));  // open: clr
  Multiplexer #(.select(5), .width(32), .enable("false")) multiplexer_1 (
    .in0({32{1'b0}}), .in1(ra), .in2(sp), .in5(t0), .in6(t1), .in7(t2), .in8(s0), .in9(s1), .in10(a0),
    .out(Read_Data_1), .sel(Read_Register_1_rs1));  // open: in3, in4, in11, in12, in13, in14, in15, in16, in17, in18, in19, in20, in21, in22, in23, in24, in25, in26, in27, in28, in29, in30, in31
  Multiplexer #(.select(5), .width(32), .enable("false")) multiplexer_2 (
    .in0(undriven), .in1(undriven_2), .in2(undriven_3), .in3(undriven_4), .in4(undriven_5), .in5(undriven_6),
    .in6(undriven_7), .in7(undriven_8), .in8(undriven_9), .in9(undriven_10), .in10(undriven_11),
    .in11(undriven_12), .in12(undriven_13), .in13(undriven_14), .in14(undriven_15), .in15(undriven_16),
    .in16(undriven_17), .in17(undriven_18), .in18(undriven_19), .in19(undriven_20), .in20(undriven_21),
    .in21(undriven_22), .in22(undriven_23), .in23(undriven_24), .in24(undriven_25), .in25(undriven_26),
    .in26(undriven_27), .in27(undriven_28), .in28(undriven_29), .in29(undriven_30), .in30(undriven_31),
    .in31(undriven_32), .out(multiplexer_2_out), .sel(undriven_33));
  Multiplexer #(.select(5), .width(32), .enable("false")) multiplexer_3 (
    .in0(undriven), .in1(undriven_2), .in2(undriven_3), .in3(undriven_4), .in4(undriven_5), .in5(undriven_6),
    .in6(undriven_7), .in7(undriven_8), .in8(undriven_9), .in9(undriven_10), .in10(undriven_11),
    .in11(undriven_12), .in12(undriven_13), .in13(undriven_14), .in14(undriven_15), .in15(undriven_16),
    .in16(undriven_17), .in17(undriven_18), .in18(undriven_19), .in19(undriven_20), .in20(undriven_21),
    .in21(undriven_22), .in22(undriven_23), .in23(undriven_24), .in24(undriven_25), .in25(undriven_26),
    .in26(undriven_27), .in27(undriven_28), .in28(undriven_29), .in29(undriven_30), .in30(undriven_31),
    .in31(undriven_32), .out(multiplexer_2_out), .sel(undriven_33));
  Multiplexer #(.select(5), .width(32), .enable("false")) multiplexer_4 (
    .in0({32{1'b0}}), .in1(ra), .in2(sp), .in3(undriven_34), .in4(undriven_35), .in5(t0), .in6(t1), .in7(t2),
    .in8(s0), .in9(s1), .in10(a0), .in11(undriven_36), .in12(undriven_37), .in13(undriven_38),
    .in14(undriven_39), .in15(undriven_40), .in16(undriven_41), .in17(undriven_42), .in18(undriven_43),
    .in19(undriven_44), .in20(undriven_45), .in21(undriven_46), .in22(undriven_47), .in23(undriven_48),
    .in24(undriven_49), .in25(undriven_50), .in26(undriven_51), .in27(undriven_52), .in28(undriven_53),
    .in29(undriven_54), .in30(undriven_55), .in31(undriven_56), .out(Read_Data_2), .sel(Read_Register_2_rs2));
  Multiplexer #(.select(5), .width(32), .enable("false")) multiplexer_5 (
    .in0({32{1'b0}}), .in1(ra), .in2(sp), .in3(undriven_34), .in4(undriven_35), .in5(t0), .in6(t1), .in7(t2),
    .in8(s0), .in9(s1), .in10(a0), .in11(undriven_36), .in12(undriven_37), .in13(undriven_38),
    .in14(undriven_39), .in15(undriven_40), .in16(undriven_41), .in17(undriven_42), .in18(undriven_43),
    .in19(undriven_44), .in20(undriven_45), .in21(undriven_46), .in22(undriven_47), .in23(undriven_48),
    .in24(undriven_49), .in25(undriven_50), .in26(undriven_51), .in27(undriven_52), .in28(undriven_53),
    .in29(undriven_54), .in30(undriven_55), .in31(undriven_56), .out(Read_Data_2), .sel(Read_Register_2_rs2));

  // Other names for the same wires on the sheet: clk = Clock; read_data1[31:0] = Read_Data_1;
  //   read_data2[31:0] = Read_Data_2; read_reg1[4:0] = Read_Register_1_rs1; read_reg2[4:0] = Read_Register_2_rs2;
  //   write_en = Write_Enable; write_reg[4:0] = Write_Register_rd

  // Notes on the sheet:
  //   INPUTS to your circuit
  //   DON'T CHANGE THE LOCATIONS OF THE INPUTS AND OUTPUTS!
  //   These are DEBUG/TEST outputs from your circuit.
  //   OUTPUTS from your circuit
endmodule
