// Logisim project regfile.circ as structural Verilog: 1 circuit, main circuit main
module main (
  input  [4:0] Read_Register_1_rs1,
  input  [4:0] Read_Register_2_rs2,
  input  [4:0] Write_Register_rd,
  input  [31:0] Write_Data,
  input  Write_Enable,
  input  Clock,
  output [31:0] ra,
  output [31:0] sp,
  output [31:0] t0,
  output [31:0] t1,
  output [31:0] t2,
  output [31:0] s0,
  output [31:0] s1,
  output [31:0] a0,
  output [31:0] Read_Data_1,
  output [31:0] Read_Data_2
);

  wire demultiplexer_1_out1, demultiplexer_1_out2, demultiplexer_1_out5, demultiplexer_1_out6,
       demultiplexer_1_out7, demultiplexer_1_out8, demultiplexer_1_out9, demultiplexer_1_out10;
  wire [31:0] undriven, undriven_2, undriven_3, undriven_4, undriven_5, undriven_6, undriven_7, undriven_8,
       undriven_9, undriven_10, undriven_11, undriven_12, undriven_13, undriven_14, undriven_15, undriven_16,
       undriven_17, undriven_18, undriven_19, undriven_20, undriven_21, undriven_22, undriven_23;

  Demultiplexer #(.select(5), .enable("false")) demultiplexer_1 (
    .out1(demultiplexer_1_out1), .out2(demultiplexer_1_out2), .out5(demultiplexer_1_out5),
    .out6(demultiplexer_1_out6), .out7(demultiplexer_1_out7), .out8(demultiplexer_1_out8),
    .out9(demultiplexer_1_out9), .out10(demultiplexer_1_out10), .in(Write_Enable), .sel(Write_Register_rd));  // open: out0, out3, out4, out11, out12, out13, out14, out15, out16, out17, out18, out19, out20, out21, out22, out23, out24, out25, out26, out27, out28, out29, out30, out31
  Register #(.width(32)) register_1 (.D(Write_Data), .en(demultiplexer_1_out1), .clk(Clock), .Q(ra));  // open: clr
  Register #(.width(32)) register_2 (.D(Write_Data), .en(demultiplexer_1_out5), .clk(Clock), .Q(t0));  // open: clr
  Register #(.width(32)) register_3 (.D(Write_Data), .en(demultiplexer_1_out7), .clk(Clock), .Q(t2));  // open: clr
  Register #(.width(32)) register_4 (.D(Write_Data), .en(demultiplexer_1_out8), .clk(Clock), .Q(s0));  // open: clr
  Register #(.width(32)) register_5 (.D(Write_Data), .en(demultiplexer_1_out9), .clk(Clock), .Q(s1));  // open: clr
  Register #(.width(32)) register_6 (.D(Write_Data), .en(demultiplexer_1_out10), .clk(Clock), .Q(a0));  // open: clr
  Register #(.width(32)) register_7 (.D(Write_Data), .en(demultiplexer_1_out2), .clk(Clock), .Q(sp));  // open: clr
  Register #(.width(32)) register_8 (.D(Write_Data), .en(demultiplexer_1_out6), .clk(Clock), .Q(t1));  // open: clr
  Multiplexer #(.select(5), .width(32), .enable("false")) multiplexer_1 (
    .in0({32{1'b0}}), .in1(ra), .in2(sp), .in5(t0), .in6(t1), .in7(t2), .in8(s0), .in9(s1), .in10(a0),
    .out(Read_Data_1), .sel(Read_Register_1_rs1));  // open: in3, in4, in11, in12, in13, in14, in15, in16, in17, in18, in19, in20, in21, in22, in23, in24, in25, in26, in27, in28, in29, in30, in31
  Multiplexer #(.select(5), .width(32), .enable("false")) multiplexer_2 (
    .in0({32{1'b0}}), .in1(ra), .in2(sp), .in3(undriven), .in4(undriven_2), .in5(t0), .in6(t1), .in7(t2),
    .in8(s0), .in9(s1), .in10(a0), .in11(undriven_3), .in12(undriven_4), .in13(undriven_5),
    .in14(undriven_6), .in15(undriven_7), .in16(undriven_8), .in17(undriven_9), .in18(undriven_10),
    .in19(undriven_11), .in20(undriven_12), .in21(undriven_13), .in22(undriven_14), .in23(undriven_15),
    .in24(undriven_16), .in25(undriven_17), .in26(undriven_18), .in27(undriven_19), .in28(undriven_20),
    .in29(undriven_21), .in30(undriven_22), .in31(undriven_23), .out(Read_Data_2), .sel(Read_Register_2_rs2));
  Multiplexer #(.select(5), .width(32), .enable("false")) multiplexer_3 (
    .in0({32{1'b0}}), .in1(ra), .in2(sp), .in3(undriven), .in4(undriven_2), .in5(t0), .in6(t1), .in7(t2),
    .in8(s0), .in9(s1), .in10(a0), .in11(undriven_3), .in12(undriven_4), .in13(undriven_5),
    .in14(undriven_6), .in15(undriven_7), .in16(undriven_8), .in17(undriven_9), .in18(undriven_10),
    .in19(undriven_11), .in20(undriven_12), .in21(undriven_13), .in22(undriven_14), .in23(undriven_15),
    .in24(undriven_16), .in25(undriven_17), .in26(undriven_18), .in27(undriven_19), .in28(undriven_20),
    .in29(undriven_21), .in30(undriven_22), .in31(undriven_23), .out(Read_Data_2), .sel(Read_Register_2_rs2));

  // Other names for the same wires on the sheet: clk = Clock; read_data1[31:0] = Read_Data_1;
  //   read_data2[31:0] = Read_Data_2; read_reg1[4:0] = Read_Register_1_rs1; read_reg2[4:0] = Read_Register_2_rs2;
  //   write_en = Write_Enable; write_reg[4:0] = Write_Register_rd

  // Notes on the sheet:
  //   INPUTS to your circuit
  //   DON'T CHANGE THE LOCATIONS OF THE INPUTS AND OUTPUTS!
  //   These are DEBUG/TEST outputs from your circuit.
  //   OUTPUTS from your circuit
endmodule
