// Logisim project alu.circ as structural Verilog: 1 circuit, main circuit alu
module alu (
  input  [31:0] A,
  input  [31:0] B,
  input  [3:0] ALUSel,
  output [31:0] Result
);

  wire comparator_1_lt;
  wire [31:0] add, myand, mydiv, mymul, mymulh, myor, myrem, mysll, myslt, mysra, mysrl, mysub, myxor;

  Adder #(.width(32)) adder_1 (.a(A), .b(B), .out(add));  // open: cin, cout
  assign myand = A & B;  // AND_Gate and_1, 32 bits wide
  assign myor = A | B;  // OR_Gate or_1, 32 bits wide
  assign myxor = A ^ B;  // XOR_Gate xor_1, 32 bits wide
  Shifter #(.width(32), .shift("lr")) shifter_1 (.in(A), .\dist (B[4:0]), .out(mysrl));
  Shifter #(.width(32), .shift("ar")) shifter_2 (.in(A), .\dist (B[4:0]), .out(mysra));
  Shifter #(.width(32)) shifter_3 (.in(A), .\dist (B[4:0]), .out(mysll));
  Comparator #(.width(32)) comparator_1 (.a(A), .b(B), .lt(comparator_1_lt));  // open: gt, eq
  Divider #(.width(32)) divider_1 (.a(A), .b(B), .out(mydiv));  // open: upper, rem
  Divider #(.width(32)) divider_2 (.a(A), .b(B), .rem(myrem));  // open: out, upper
  Multiplier #(.width(32)) multiplier_1 (.a(A), .b(B), .out(mymul));  // open: cin, cout
  Multiplier #(.width(32)) multiplier_2 (.a(A), .b(B), .cout(mymulh));  // open: out, cin
  Subtractor #(.width(32)) subtractor_1 (.a(A), .b(B), .out(mysub));  // open: bin, bout
  assign myslt = {{31{1'b0}}, comparator_1_lt};  // Bit_Extender bit_extender_1
  Multiplexer #(.select(4), .width(32), .enable("false")) multiplexer_1 (
    .in0(add), .in1(myand), .in2(myor), .in3(myxor), .in4(mysrl), .in5(mysra), .in6(mysll), .in7(myslt),
    .in8(mydiv), .in9(myrem), .in10(mymul), .in11(mymulh), .in12(mysub), .in13(B), .out(Result), .sel(ALUSel));  // open: in14, in15

  // Other names for the same wires on the sheet: mybsel[31:0] = B

  // Notes on the sheet:
  //   INPUTS to your circuit
  //   DON'T CHANGE THE LOCATIONS OF THE INPUTS AND OUTPUTS!
  //   OUTPUT from your circuit
endmodule
