// Logisim project cpu.circ as structural Verilog: 5 circuits, main circuit main
module main (
  input  [31:0] INSTRUCTION,
  input  in_2,
  output [31:0] FETCH_ADDRESS,
  output [31:0] ra,
  output [31:0] sp,
  output [31:0] t0,
  output [31:0] t1,
  output [31:0] t2,
  output [31:0] s0,
  output [31:0] s1,
  output [31:0] a0
);

  wire and_1_out, ASel, BrEq, BrLT, BrUn, BSel, comparator_1_eq, comparator_2_eq, comparator_3_eq, MemRW,
       or_1_out, PCSel, RegWEn;
  wire [1:0] WBSel;
  wire [2:0] ImmSel;
  wire [3:0] ALUSel;
  wire [31:0] adder_1_out, adder_2_out, AluOut, inst, IO, load_1_loaded, MEM_p5, multiplexer_1_out,
       multiplexer_2_out, multiplexer_3_out, multiplexer_4_out, PC, PC_q, R1, R2, WD;

  Adder #(.width(32)) adder_1 (.a(PC_q), .b(32'h4), .out(adder_1_out));  // open: cin, cout
  Multiplexer #(.width(32), .enable("false")) multiplexer_1 (
    .in0(adder_1_out), .in1(AluOut), .out(multiplexer_1_out), .sel(PCSel));
  Register #(.width(32)) u_PC (.D(multiplexer_1_out), .clk(in_2), .Q(PC_q));  // open: en, clr
  Comparator #(.width(3)) comparator_1 (.a(ImmSel), .b(3'b100), .eq(comparator_1_eq));  // open: gt, lt
  Comparator #(.width(3)) comparator_2 (.a(ImmSel), .b(3'b110), .eq(comparator_2_eq));  // open: gt, lt
  Comparator #(.width(3)) comparator_3 (.a(ImmSel), .b(3'b111), .eq(comparator_3_eq));  // open: gt, lt
  and and_1 (and_1_out, PCSel, comparator_1_eq);
  Register #(.width(32)) register_1 (.D(PC_q), .clk(in_2), .Q(PC));  // open: en, clr
  Shifter #(.width(32), .shift("ar")) shifter_1 (.in(PC_q), .\dist (5'b00010), .out(FETCH_ADDRESS));
  Multiplexer #(.width(32), .enable("false")) multiplexer_2 (
    .in0(INSTRUCTION), .in1({32{1'b0}}), .out(multiplexer_2_out), .sel(or_1_out));
  or or_1 (or_1_out, and_1_out, comparator_2_eq, comparator_3_eq);
  Register #(.width(32)) register_2 (.D(multiplexer_2_out), .clk(in_2), .Q(inst));  // open: en, clr
  ImmGen immgen_1 (.immInput(inst[31:7]), .ImmSel(ImmSel), .ImmOut(IO));
  regfile_main main_1 (
    .Read_Register_1_rs1(inst[19:15]), .Read_Register_2_rs2(inst[24:20]), .Write_Register_rd(inst[11:7]),
    .Write_Data(WD), .Write_Enable(RegWEn), .Clock(in_2), .Read_Data_1(R1), .Read_Data_2(R2), .ra(ra),
    .sp(sp), .t0(t0), .t1(t1), .t2(t2), .s0(s0), .s1(s1), .a0(a0));
  control control_1 (
    .inst(inst), .BrEq(BrEq), .BrLT(BrLT), .MemRW(MemRW), .BrUn(BrUn), .RegWEn(RegWEn), .ASel(ASel),
    .ALUSel(ALUSel), .BSel(BSel), .ImmSel(ImmSel), .PCSel(PCSel), .WBSel(WBSel));
  BranchComp branchcomp_1 (.RS1(R1), .RS2(R2), .BrUn(BrUn), .BrEq(BrEq), .BrLT(BrLT));
  Multiplexer #(.width(32), .enable("false")) multiplexer_3 (.in0(R1), .in1(PC), .out(multiplexer_3_out), .sel(ASel));
  Multiplexer #(.width(32), .enable("false")) multiplexer_4 (.in0(R2), .in1(IO), .out(multiplexer_4_out), .sel(BSel));
  alu alu_1 (.A(multiplexer_3_out), .B(multiplexer_4_out), .ALUSel(ALUSel), .Result(AluOut));
  Adder #(.width(32)) adder_2 (.a(32'h4), .b(PC), .out(adder_2_out));  // open: cin, cout
  // mem_main MEM: pin names not known; wires that end beside it: AluOut, R2, MemRW, in_2, MEM_p5
  load load_1 (.data(MEM_p5), .inst(inst), .ALUOut(AluOut), .loaded(load_1_loaded));
  Multiplexer #(.select(2), .width(32), .enable("false")) multiplexer_5 (
    .in0(adder_2_out), .in1(AluOut), .in2(load_1_loaded), .out(WD), .sel(WBSel));  // open: in3

  // Other names for the same wires on the sheet: clk = in_2; fetch_addr[31:0] = FETCH_ADDRESS

  // Notes on the sheet:
  //   Output
  //   Inputs/Outputs from run.circ. DO NOT MOVE THESE.
  //   Inputs
  //   It is OK to move the PC, RegFile, ALU, and MEM to wherever is most convenient for you when constructing your CPU, and to delete this text
  //   Inputs/Outputs from run.circ. DO NOT MOVE THESE.
endmodule

module ImmGen (
  input  [24:0] immInput,
  input  [2:0] ImmSel,
  output [31:0] ImmOut
);

  wire [31:0] B, I, jalr, S, UJ;

  assign I = {{20{immInput[24]}}, immInput[24:13]};  // Bit_Extender bit_extender_1
  assign S = {{20{immInput[24]}}, {immInput[24:18], immInput[4:0]}};  // Bit_Extender bit_extender_2
  assign B = {{19{immInput[24]}}, {immInput[24], immInput[0], immInput[23:18], immInput[4:1], 1'b0}};  // Bit_Extender bit_extender_3
  assign UJ = {{11{immInput[24]}}, {immInput[24], immInput[12:5], immInput[13], immInput[23:14], 1'b0}};  // Bit_Extender bit_extender_4
  assign jalr = {{20{immInput[24]}}, immInput[24:13]};  // Bit_Extender bit_extender_5
  Multiplexer #(.select(3), .width(32), .enable("false")) multiplexer_1 (
    .in0({32{1'b0}}), .in1(I), .in3(S), .in4(B), .in5({immInput[24:5], {12{1'b0}}}), .in6(UJ), .in7(jalr),
    .out(ImmOut), .sel(ImmSel));  // open: in2

  // Other names for the same wires on the sheet: U[31:12] = immInput[24:5]
endmodule

module BranchComp (
  input  [31:0] RS1,
  input  [31:0] RS2,
  input  BrUn,
  output BrEq,
  output BrLT
);

  wire BrLTSigned, comparator_1_eq, comparator_2_eq, comparator_2_lt;

  Comparator #(.width(32)) comparator_1 (.a(RS1), .b(RS2), .eq(comparator_1_eq), .lt(BrLTSigned));  // open: gt
  Comparator #(.width(32), .mode("unsigned")) comparator_2 (
    .a(RS1), .b(RS2), .eq(comparator_2_eq), .lt(comparator_2_lt));  // open: gt
  Multiplexer #(.enable("false")) multiplexer_1 (.in0(comparator_1_eq), .in1(comparator_2_eq), .out(BrEq), .sel(BrUn));
  Multiplexer #(.enable("false")) multiplexer_2 (.in0(BrLTSigned), .in1(comparator_2_lt), .out(BrLT), .sel(BrUn));

  // Other names for the same wires on the sheet: a[31:0] = RS1; b[31:0] = RS2
endmodule

module control (
  input  [31:0] inst,
  input  BrEq,
  input  BrLT,
  output MemRW,
  output BrUn,
  output RegWEn,
  output ASel,
  output [3:0] ALUSel,
  output BSel,
  output [2:0] ImmSel,
  output PCSel,
  output [1:0] WBSel
);

  wire Add, and_10_out, and_11_out, and_12_out, and_13_out, and_14_out, and_15_out, and_19_out, and_20_out,
       and_21_out, and_22_out, and_24_out, and_25_out, and_26_out, and_27_out, and_28_out, and_29_out,
       and_30_out, and_31_out, and_37_out, and_38_out, and_39_out, and_40_out, I, imm0, imm1, imm20, jalr,
       load, myAnd, myBsel, myDiv, myMul, myMulh, myOr, myRem, mySll, mySlt, mySra, mySrl, mySub, myXor,
       not_2_out, or_3_out, or_4_out, or_14_out, R, SB, Seven0, Seven1, Seven20, Srli, Three0, Three1,
       Three2, Three3, Three4, Three5, Three6, Three7, UJ;
  wire [1:0] and_16_out, and_17_out, and_18_out, bit_extender_8_out, bit_extender_9_out, bit_extender_10_out;
  wire [2:0] and_2_out, and_3_out, and_4_out, and_5_out, and_6_out, and_7_out, and_8_out, bit_extender_1_out,
       bit_extender_2_out, bit_extender_3_out, bit_extender_4_out, bit_extender_5_out, bit_extender_6_out,
       bit_extender_7_out;
  wire [3:0] and_41_out, and_42_out, and_43_out, and_44_out, and_45_out, and_46_out, and_47_out, and_48_out,
       and_49_out, and_50_out, and_51_out, and_52_out, and_53_out, and_54_out, bit_extender_11_out,
       bit_extender_12_out, bit_extender_13_out, bit_extender_14_out, bit_extender_15_out,
       bit_extender_16_out, bit_extender_17_out, bit_extender_18_out, bit_extender_19_out,
       bit_extender_20_out, bit_extender_21_out, bit_extender_22_out, bit_extender_23_out,
       bit_extender_24_out;

  Comparator #(.width(7), .mode("unsigned")) comparator_1 (.a(inst[6:0]), .b(7'b0110011), .eq(R));  // open: gt, lt
  Comparator #(.width(7), .mode("unsigned")) comparator_2 (.a(inst[6:0]), .b(7'b0000011), .eq(load));  // open: gt, lt
  Comparator #(.width(7), .mode("unsigned")) comparator_3 (.a(inst[6:0]), .b(7'b0010011), .eq(I));  // open: gt, lt
  Comparator #(.width(7), .mode("unsigned")) comparator_4 (.a(inst[6:0]), .b(7'b0100011), .eq(MemRW));  // open: gt, lt
  Comparator #(.width(7), .mode("unsigned")) comparator_5 (.a(inst[6:0]), .b(7'b1100011), .eq(SB));  // open: gt, lt
  Comparator #(.width(7), .mode("unsigned")) comparator_6 (.a(inst[6:0]), .b(7'b0110111), .eq(myBsel));  // open: gt, lt
  Comparator #(.width(7), .mode("unsigned")) comparator_7 (.a(inst[6:0]), .b(7'b1101111), .eq(UJ));  // open: gt, lt
  Comparator #(.width(7), .mode("unsigned")) comparator_8 (.a(inst[6:0]), .b(7'b1100111), .eq(jalr));  // open: gt, lt
  Comparator #(.width(3), .mode("unsigned")) comparator_9 (.a(inst[14:12]), .b(3'b000), .eq(Three0));  // open: gt, lt
  Comparator #(.width(3), .mode("unsigned")) comparator_10 (.a(inst[14:12]), .b(3'b001), .eq(Three1));  // open: gt, lt
  Comparator #(.width(3), .mode("unsigned")) comparator_11 (.a(inst[14:12]), .b(3'b010), .eq(Three2));  // open: gt, lt
  Comparator #(.width(3), .mode("unsigned")) comparator_12 (.a(inst[14:12]), .b(3'b011), .eq(Three3));  // open: gt, lt
  Comparator #(.width(3), .mode("unsigned")) comparator_13 (.a(inst[14:12]), .b(3'b100), .eq(Three4));  // open: gt, lt
  Comparator #(.width(3), .mode("unsigned")) comparator_14 (.a(inst[14:12]), .b(3'b101), .eq(Three5));  // open: gt, lt
  Comparator #(.width(3), .mode("unsigned")) comparator_15 (.a(inst[14:12]), .b(3'b110), .eq(Three6));  // open: gt, lt
  Comparator #(.width(3), .mode("unsigned")) comparator_16 (.a(inst[14:12]), .b(3'b111), .eq(Three7));  // open: gt, lt
  Comparator #(.width(12), .mode("unsigned")) comparator_17 (
    .a(inst[31:20]), .b({12{1'b0}}), .eq(imm0));  // open: gt, lt
  Comparator #(.width(12), .mode("unsigned")) comparator_18 (.a(inst[31:20]), .b(12'h1), .eq(imm1));  // open: gt, lt
  Comparator #(.width(12), .mode("unsigned")) comparator_19 (.a(inst[31:20]), .b(12'h20), .eq(imm20));  // open: gt, lt
  Comparator #(.width(7), .mode("unsigned")) comparator_20 (
    .a(inst[31:25]), .b({7{1'b0}}), .eq(Seven0));  // open: gt, lt
  Comparator #(.width(7), .mode("unsigned")) comparator_21 (
    .a(inst[31:25]), .b(7'b0000001), .eq(Seven1));  // open: gt, lt
  Comparator #(.width(7), .mode("unsigned")) comparator_22 (
    .a(inst[31:25]), .b(7'b0100000), .eq(Seven20));  // open: gt, lt
  and and_1 (Srli, Three5, Seven1, I);
  assign bit_extender_1_out = {{2{I}}, I};  // Bit_Extender bit_extender_1
  assign bit_extender_2_out = {{2{jalr}}, jalr};  // Bit_Extender bit_extender_2
  assign bit_extender_3_out = {{2{load}}, load};  // Bit_Extender bit_extender_3
  assign bit_extender_4_out = {{2{MemRW}}, MemRW};  // Bit_Extender bit_extender_4
  assign bit_extender_5_out = {{2{SB}}, SB};  // Bit_Extender bit_extender_5
  assign bit_extender_6_out = {{2{myBsel}}, myBsel};  // Bit_Extender bit_extender_6
  assign bit_extender_7_out = {{2{UJ}}, UJ};  // Bit_Extender bit_extender_7
  assign and_2_out = 3'b001 & bit_extender_1_out;  // AND_Gate and_2, 3 bits wide
  assign and_3_out = 3'b001 & bit_extender_2_out;  // AND_Gate and_3, 3 bits wide
  assign and_4_out = 3'b001 & bit_extender_3_out;  // AND_Gate and_4, 3 bits wide
  assign and_5_out = bit_extender_4_out & 3'b011;  // AND_Gate and_5, 3 bits wide
  assign and_6_out = bit_extender_5_out & 3'b100;  // AND_Gate and_6, 3 bits wide
  assign and_7_out = bit_extender_6_out & 3'b101;  // AND_Gate and_7, 3 bits wide
  assign and_8_out = bit_extender_7_out & 3'b110;  // AND_Gate and_8, 3 bits wide
  assign ImmSel = and_2_out | and_3_out | and_4_out | and_5_out | and_6_out | and_7_out | and_8_out;  // OR_Gate or_1, 3 bits wide
  and and_9 (BrUn, SB, Three6);
  or or_2 (ASel, SB, UJ);
  not not_1 (BSel, R);
  or or_3 (or_3_out, R, myBsel, I);
  or or_4 (or_4_out, UJ, jalr);
  and and_10 (and_10_out, R, Three0, Seven0);
  and and_11 (and_11_out, I, Three0);
  and and_12 (and_12_out, R, Three7, Seven0);
  and and_13 (and_13_out, I, Three7);
  and and_14 (and_14_out, R, Three6, Seven0);
  and and_15 (and_15_out, I, Three6);
  assign bit_extender_8_out = {{1{or_3_out}}, or_3_out};  // Bit_Extender bit_extender_8
  assign and_16_out = bit_extender_8_out & 2'b01;  // AND_Gate and_16, 2 bits wide
  assign bit_extender_9_out = {{1{load}}, load};  // Bit_Extender bit_extender_9
  assign and_17_out = bit_extender_9_out & 2'b10;  // AND_Gate and_17, 2 bits wide
  assign bit_extender_10_out = {{1{or_4_out}}, or_4_out};  // Bit_Extender bit_extender_10
  assign and_18_out = bit_extender_10_out & 2'b00;  // AND_Gate and_18, 2 bits wide
  or or_5 (Add, and_10_out, load, and_11_out, MemRW, SB, UJ, jalr);
  or or_6 (myAnd, and_12_out, and_13_out);
  or or_7 (myOr, and_14_out, and_15_out);
  assign WBSel = and_16_out | and_17_out | and_18_out;  // OR_Gate or_8, 2 bits wide
  and and_19 (and_19_out, R, Three4, Seven0);
  and and_20 (and_20_out, I, Three4);
  and and_21 (and_21_out, R, Three5, Seven0);
  and and_22 (and_22_out, I, Three5, imm0);
  and and_23 (mySra, I, Three5, imm20);
  and and_24 (and_24_out, R, Three1, Seven0);
  and and_25 (and_25_out, I, Three1);
  or or_9 (myXor, and_19_out, and_20_out);
  or or_10 (mySrl, and_21_out, and_22_out);
  or or_11 (mySll, and_24_out, and_25_out);
  and and_26 (and_26_out, SB, Three0);
  and and_27 (and_27_out, SB, Three4);
  and and_28 (and_28_out, SB, Three1);
  not not_2 (not_2_out, BrEq);
  and and_29 (and_29_out, SB, Three6);
  and and_30 (and_30_out, R, Three2, Seven0);
  and and_31 (and_31_out, I, Three2);
  and and_32 (myDiv, R, Three4, Seven1);
  and and_33 (myRem, R, Three6, Seven1);
  and and_34 (myMul, R, Three0, Seven1);
  and and_35 (myMulh, R, Three1, Seven1);
  and and_36 (mySub, R, Three0, Seven20);
  and and_37 (and_37_out, and_26_out, BrEq);
  and and_38 (and_38_out, and_27_out, BrLT);
  and and_39 (and_39_out, and_28_out, not_2_out);
  and and_40 (and_40_out, and_29_out, BrLT);
  or or_12 (mySlt, and_30_out, and_31_out);
  or or_13 (PCSel, and_37_out, and_38_out, and_39_out, and_40_out, UJ, jalr);
  not not_3 (RegWEn, or_14_out);
  or or_14 (or_14_out, MemRW, SB);
  assign bit_extender_11_out = {{3{Add}}, Add};  // Bit_Extender bit_extender_11
  assign bit_extender_12_out = {{3{myAnd}}, myAnd};  // Bit_Extender bit_extender_12
  assign and_41_out = bit_extender_12_out & 4'b0001;  // AND_Gate and_41, 4 bits wide
  assign bit_extender_13_out = {{3{myOr}}, myOr};  // Bit_Extender bit_extender_13
  assign and_42_out = bit_extender_13_out & 4'b0010;  // AND_Gate and_42, 4 bits wide
  assign bit_extender_14_out = {{3{myXor}}, myXor};  // Bit_Extender bit_extender_14
  assign and_43_out = bit_extender_14_out & 4'b0011;  // AND_Gate and_43, 4 bits wide
  assign bit_extender_15_out = {{3{mySrl}}, mySrl};  // Bit_Extender bit_extender_15
  assign and_44_out = bit_extender_15_out & 4'b0100;  // AND_Gate and_44, 4 bits wide
  assign bit_extender_16_out = {{3{mySra}}, mySra};  // Bit_Extender bit_extender_16
  assign and_45_out = bit_extender_16_out & 4'b0101;  // AND_Gate and_45, 4 bits wide
  assign bit_extender_17_out = {{3{mySll}}, mySll};  // Bit_Extender bit_extender_17
  assign and_46_out = bit_extender_17_out & 4'b0110;  // AND_Gate and_46, 4 bits wide
  assign bit_extender_18_out = {{3{mySlt}}, mySlt};  // Bit_Extender bit_extender_18
  assign and_47_out = bit_extender_18_out & 4'b0111;  // AND_Gate and_47, 4 bits wide
  assign bit_extender_19_out = {{3{myDiv}}, myDiv};  // Bit_Extender bit_extender_19
  assign and_48_out = bit_extender_19_out & 4'b1000;  // AND_Gate and_48, 4 bits wide
  assign bit_extender_20_out = {{3{myRem}}, myRem};  // Bit_Extender bit_extender_20
  assign and_49_out = bit_extender_20_out & 4'b1001;  // AND_Gate and_49, 4 bits wide
  assign bit_extender_21_out = {{3{myMul}}, myMul};  // Bit_Extender bit_extender_21
  assign and_50_out = bit_extender_21_out & 4'b1010;  // AND_Gate and_50, 4 bits wide
  assign bit_extender_22_out = {{3{myMulh}}, myMulh};  // Bit_Extender bit_extender_22
  assign and_51_out = bit_extender_22_out & 4'b1011;  // AND_Gate and_51, 4 bits wide
  assign bit_extender_23_out = {{3{mySub}}, mySub};  // Bit_Extender bit_extender_23
  assign and_52_out = bit_extender_23_out & 4'b1100;  // AND_Gate and_52, 4 bits wide
  assign bit_extender_24_out = {{3{myBsel}}, myBsel};  // Bit_Extender bit_extender_24
  assign and_53_out = bit_extender_24_out & 4'b1101;  // AND_Gate and_53, 4 bits wide
  assign and_54_out = bit_extender_11_out & 4'b0000;  // AND_Gate and_54, 4 bits wide
  assign ALUSel = and_54_out | and_41_out | and_42_out | and_43_out | and_44_out | and_45_out | and_46_out | and_47_out | and_48_out | and_49_out | and_50_out | and_51_out | and_52_out | and_53_out;  // OR_Gate or_15, 4 bits wide

  // Other names for the same wires on the sheet: imm[11:0] = inst[31:20]; funct7[6:0] = inst[31:25];
  //   Opcode[6:0] = inst[6:0]; funct3[2:0] = inst[14:12]; U = myBsel; S = MemRW
endmodule

module load (
  input  [31:0] data,
  input  [31:0] inst,
  input  [31:0] ALUOut,
  output [31:0] loaded
);

  wire comparator_1_eq, comparator_2_eq, comparator_3_eq, comparator_4_eq, comparator_8_eq, comparator_9_eq,
       lb, lh, lw;
  wire [7:0] and_1_out, and_2_out, and_3_out, and_4_out, bit_extender_1_out, bit_extender_2_out,
       bit_extender_3_out, bit_extender_4_out;
  wire [15:0] and_8_out, and_9_out, bit_extender_12_out, bit_extender_13_out;
  wire [31:0] and_5_out, and_6_out, and_7_out, bit_extender_5_out, bit_extender_6_out, bit_extender_7_out,
       bit_extender_8_out, bit_extender_9_out, bit_extender_10_out, bit_extender_11_out, bit_extender_14_out,
       bit_extender_15_out, byteOffset, hwOffset, lbresult, lhresult;

  Comparator #(.width(32)) comparator_1 (.a(byteOffset), .b({32{1'b0}}), .eq(comparator_1_eq));  // open: gt, lt
  Comparator #(.width(32)) comparator_2 (.a(byteOffset), .b(32'h1), .eq(comparator_2_eq));  // open: gt, lt
  Comparator #(.width(32)) comparator_3 (.a(byteOffset), .b(32'h2), .eq(comparator_3_eq));  // open: gt, lt
  Comparator #(.width(32)) comparator_4 (.a(byteOffset), .b(32'h3), .eq(comparator_4_eq));  // open: gt, lt
  Divider #(.width(32)) divider_1 (.a(ALUOut), .b(32'h4), .rem(byteOffset));  // open: out, upper
  Divider #(.width(32)) divider_2 (.a(ALUOut), .b(32'h2), .rem(hwOffset));  // open: out, upper
  assign bit_extender_1_out = {{7{comparator_1_eq}}, comparator_1_eq};  // Bit_Extender bit_extender_1
  assign bit_extender_2_out = {{7{comparator_2_eq}}, comparator_2_eq};  // Bit_Extender bit_extender_2
  assign bit_extender_3_out = {{7{comparator_3_eq}}, comparator_3_eq};  // Bit_Extender bit_extender_3
  assign bit_extender_4_out = {{7{comparator_4_eq}}, comparator_4_eq};  // Bit_Extender bit_extender_4
  assign and_1_out = data[7:0] & bit_extender_1_out;  // AND_Gate and_1, 8 bits wide
  assign and_2_out = bit_extender_2_out & data[15:8];  // AND_Gate and_2, 8 bits wide
  assign and_3_out = data[23:16] & bit_extender_3_out;  // AND_Gate and_3, 8 bits wide
  assign and_4_out = bit_extender_4_out & data[31:24];  // AND_Gate and_4, 8 bits wide
  Comparator #(.width(3)) comparator_5 (.a(inst[14:12]), .b(3'b000), .eq(lb));  // open: gt, lt
  Comparator #(.width(3)) comparator_6 (.a(inst[14:12]), .b(3'b001), .eq(lh));  // open: gt, lt
  Comparator #(.width(3)) comparator_7 (.a(inst[14:12]), .b(3'b010), .eq(lw));  // open: gt, lt
  assign bit_extender_5_out = {{24{and_1_out[7]}}, and_1_out};  // Bit_Extender bit_extender_5
  assign bit_extender_6_out = {{24{and_2_out[7]}}, and_2_out};  // Bit_Extender bit_extender_6
  assign bit_extender_7_out = {{24{and_3_out[7]}}, and_3_out};  // Bit_Extender bit_extender_7
  assign bit_extender_8_out = {{24{and_4_out[7]}}, and_4_out};  // Bit_Extender bit_extender_8
  assign bit_extender_9_out = {{31{lb}}, lb};  // Bit_Extender bit_extender_9
  assign and_5_out = bit_extender_9_out & lbresult;  // AND_Gate and_5, 32 bits wide
  assign bit_extender_10_out = {{31{lh}}, lh};  // Bit_Extender bit_extender_10
  assign and_6_out = bit_extender_10_out & lhresult;  // AND_Gate and_6, 32 bits wide
  assign bit_extender_11_out = {{31{lw}}, lw};  // Bit_Extender bit_extender_11
  assign and_7_out = bit_extender_11_out & data;  // AND_Gate and_7, 32 bits wide
  assign lbresult = bit_extender_5_out | bit_extender_6_out | bit_extender_7_out | bit_extender_8_out;  // OR_Gate or_1, 32 bits wide
  assign loaded = and_5_out | and_6_out | and_7_out;  // OR_Gate or_2, 32 bits wide
  Comparator #(.width(32)) comparator_8 (.a(hwOffset), .b({32{1'b0}}), .eq(comparator_8_eq));  // open: gt, lt
  Comparator #(.width(32)) comparator_9 (.a(hwOffset), .b(32'h1), .eq(comparator_9_eq));  // open: gt, lt
  assign bit_extender_12_out = {{15{comparator_8_eq}}, comparator_8_eq};  // Bit_Extender bit_extender_12
  assign bit_extender_13_out = {{15{comparator_9_eq}}, comparator_9_eq};  // Bit_Extender bit_extender_13
  assign and_8_out = data[15:0] & bit_extender_12_out;  // AND_Gate and_8, 16 bits wide
  assign and_9_out = bit_extender_13_out & data[31:16];  // AND_Gate and_9, 16 bits wide
  assign bit_extender_14_out = {{16{and_8_out[15]}}, and_8_out};  // Bit_Extender bit_extender_14
  assign bit_extender_15_out = {{16{and_9_out[15]}}, and_9_out};  // Bit_Extender bit_extender_15
  assign lhresult = bit_extender_14_out | bit_extender_15_out;  // OR_Gate or_3, 32 bits wide

  // Other names for the same wires on the sheet: Byte1[7:0] = data[7:0]; Half1[15:0] = data[15:0];
  //   Byte2[7:0] = data[15:8]; Byte3[7:0] = data[23:16]; Half2[15:0] = data[31:16]; Byte4[7:0] = data[31:24];
  //   funct3[2:0] = inst[14:12]
endmodule
